// Logisim project Lab_2_Solutions_Part3.circ as structural Verilog: 2 circuits, main circuit main
module main (
  input  b1,
  input  b2,
  input  b3,
  input  cin,
  input  b0,
  input  a0,
  input  a1,
  input  a2,
  input  a3,
  output cout,
  output s0,
  output s1,
  output s2,
  output s3
);

  wire FA0_cout, FA1_cout, FA2_cout;

  Full_Adder_1bit FA0 (.cin(cin), .a(b0), .b(a0), .cout(FA0_cout), .s(s0));
  Full_Adder_1bit FA1 (.cin(FA0_cout), .a(b1), .b(a1), .cout(FA1_cout), .s(s1));
  Full_Adder_1bit FA2 (.cin(FA1_cout), .a(b2), .b(a2), .cout(FA2_cout), .s(s2));
  Full_Adder_1bit full_adder_1bit_1 (.cin(FA2_cout), .a(b3), .b(a3), .cout(cout), .s(s3));
endmodule

module Full_Adder_1bit (
  input  cin,
  input  a,
  input  b,
  output cout,
  output s
);

  wire xor_1_out;

  xor xor_1 (xor_1_out, a, b);
  Multiplexer multiplexer_1 (.in0(b), .in1(cin), .out(cout), .sel(xor_1_out));
  xor xor_2 (s, cin, xor_1_out);
endmodule
