// Logisim project Lab_2_Solutions_Part4.circ as structural Verilog: 5 circuits, main circuit main
module main (
  input  cin,
  input  b0,
  input  b1,
  input  b2,
  input  b3,
  input  a0,
  input  a1,
  input  a2,
  input  a3,
  input  in_10,
  input  [3:0] Zero,
  input  [3:0] Six,
  output out_13,
  output S03,
  output S02,
  output S01,
  output S00,
  output S10
);

  wire cout, cs0, cs1, cs2, cs3, z0, z1, z2, z3;

  Multiplexer #(.width(4)) multiplexer_1 (.in0(Zero), .in1(Six), .out({cs3, cs2, cs1, cs0}), .sel(S10));
  Adder_4bit Adder_4bit_1 (
    .cin(cin), .b0(b0), .b1(b1), .b2(b2), .b3(b3), .a0(a0), .a1(a1), .a2(a2), .a3(a3), .cout(cout), .s3(z3),
    .s2(z2), .s1(z1), .s0(z0));
  BCD_Correction bcd_correction_1 (.k(cout), .z1(z1), .z2(z2), .z3(z3), .S1(S10));
  Adder_4bit adder_4bit_1_dup2 (
    .cin(in_10), .b0(cs0), .b1(cs1), .b2(cs2), .b3(cs3), .a0(z0), .a1(z1), .a2(z2), .a3(z3), .cout(out_13),
    .s3(S03), .s2(S02), .s1(S01), .s0(S00));

  // Other names for the same wires on the sheet: mux_select = S10
endmodule

module Full_Adder_1bit (
  input  cin,
  input  a,
  input  b,
  output cout,
  output s
);

  wire xor_1_out;

  xor xor_1 (xor_1_out, a, b);
  Multiplexer multiplexer_1 (.in0(b), .in1(cin), .out(cout), .sel(xor_1_out));
  xor xor_2 (s, cin, xor_1_out);
endmodule

module Adder_4bit (
  input  cin,
  input  b0,
  input  b1,
  input  b2,
  input  b3,
  input  a0,
  input  a1,
  input  a2,
  input  a3,
  output cout,
  output s3,
  output s2,
  output s1,
  output s0
);

  wire FA0_cout, FA1_cout, FA2_cout;

  Full_Adder_1bit FA0 (.cin(cin), .a(b0), .b(a0), .cout(FA0_cout), .s(s0));
  Full_Adder_1bit FA1 (.cin(FA0_cout), .a(b1), .b(a1), .cout(FA1_cout), .s(s1));
  Full_Adder_1bit FA2 (.cin(FA1_cout), .a(b2), .b(a2), .cout(FA2_cout), .s(s2));
  Full_Adder_1bit full_adder_1bit_1 (.cin(FA2_cout), .a(b3), .b(a3), .cout(cout), .s(s3));
endmodule

module myComparator (
  input  v3,
  input  v2,
  input  v1,
  input  v0,
  output z
);

  wire and_1_out, and_2_out;

  and and_1 (and_1_out, v3, v1);
  and and_2 (and_2_out, v3, v2);
  or or_1 (z, and_1_out, and_2_out);
endmodule

module BCD_Correction (
  input  k,
  input  z1,
  input  z2,
  input  z3,
  output S1
);

  wire and_1_out, and_2_out;

  and and_1 (and_1_out, z1, z3);
  and and_2 (and_2_out, z2, z3);
  or or_1 (S1, k, and_1_out, and_2_out);
endmodule
