// Logisim project Lab_2_Solutions_Part5.circ as structural Verilog: 6 circuits, main circuit main
module main (
  input  in_1,
  input  B00,
  input  B01,
  input  B02,
  input  B03,
  input  A00,
  input  A01,
  input  A02,
  input  A03,
  input  [3:0] Zero,
  input  [3:0] Six,
  input  B10,
  input  B11,
  input  B12,
  input  B13,
  input  A10,
  input  A11,
  input  A12,
  input  A13,
  input  [3:0] in_20,
  input  [3:0] in_21
);

  wire c0, c1, c2, c3, c4, c5, c6, Cout, d0, d1, d2, d3, d4, d5, d6, k, S00, s0, S01, s1, S02, s2, S03, s3,
       s4, s5, s6, S10, S11, S12, S13;
  wire [7:7] Display_1_o_seg, Display_2_o_seg, Display_3_o_seg;

  BCD_Adder Adder1 (
    .cin(in_1), .b0(B00), .b1(B01), .b2(B02), .b3(B03), .a0(A00), .a1(A01), .a2(A02), .a3(A03), .Zero(Zero),
    .Six(Six), .S03(S03), .S02(S02), .S01(S01), .S00(S00), .Cout(k));  // open: Zero_Cin, Zero_Cout
  BCD_Adder Adder2 (
    .cin(k), .b0(B10), .b1(B11), .b2(B12), .b3(B13), .a0(A10), .a1(A11), .a2(A12), .a3(A13), .Zero(in_20),
    .Six(in_21), .S03(S13), .S02(S12), .S01(S11), .S00(S10), .Cout(Cout));  // open: Zero_Cin, Zero_Cout
  _7_Segment_Display #(.active("false")) Hundreds (.g(c6), .f(c5), .a(c0), .b(c1), .e(c4), .d(c3), .c(c2), .dp(1'b1));
  _7_Segment_Display #(.active("false")) Tens (.g(s6), .f(s5), .a(s0), .b(s1), .e(s4), .d(s3), .c(s2), .dp(1'b1));
  _7_Segment_Display #(.active("false")) Ones (.g(d6), .f(d5), .a(d0), .b(d1), .e(d4), .d(d3), .c(d2), .dp(1'b1));
  Seg7_Decoder Display_1 (
    .i_m3(S13), .i_m2(S12), .i_m1(S11), .i_m0(S10), .o_seg({Display_1_o_seg[7], s6, s5, s4, s3, s2, s1, s0}));
  Seg7_Decoder Display_3 (
    .i_m0(Cout), .o_seg({Display_3_o_seg[7], c6, c5, c4, c3, c2, c1, c0}));  // open: i_m3, i_m2, i_m1
  Seg7_Decoder Display_2 (
    .i_m3(S03), .i_m2(S02), .i_m1(S01), .i_m0(S00), .o_seg({Display_2_o_seg[7], d6, d5, d4, d3, d2, d1, d0}));
endmodule

module Full_Adder_1bit (
  input  cin,
  input  a,
  input  b,
  output cout,
  output s
);

  wire xor_1_out;

  xor xor_1 (xor_1_out, a, b);
  Multiplexer multiplexer_1 (.in0(b), .in1(cin), .out(cout), .sel(xor_1_out));
  xor xor_2 (s, cin, xor_1_out);
endmodule

module Adder_4bit (
  input  cin,
  input  b0,
  input  b1,
  input  b2,
  input  b3,
  input  a0,
  input  a1,
  input  a2,
  input  a3,
  output cout,
  output s3,
  output s2,
  output s1,
  output s0
);

  wire FA0_cout, FA1_cout, FA2_cout;

  Full_Adder_1bit FA0 (.cin(cin), .a(b0), .b(a0), .cout(FA0_cout), .s(s0));
  Full_Adder_1bit FA1 (.cin(FA0_cout), .a(b1), .b(a1), .cout(FA1_cout), .s(s1));
  Full_Adder_1bit FA2 (.cin(FA1_cout), .a(b2), .b(a2), .cout(FA2_cout), .s(s2));
  Full_Adder_1bit full_adder_1bit_1 (.cin(FA2_cout), .a(b3), .b(a3), .cout(cout), .s(s3));
endmodule

module BCD_Adder (
  input  cin,
  input  b0,
  input  b1,
  input  b2,
  input  b3,
  input  a0,
  input  a1,
  input  a2,
  input  a3,
  input  Zero_Cin,
  input  [3:0] Zero,
  input  [3:0] Six,
  output Zero_Cout,
  output S03,
  output S02,
  output S01,
  output S00,
  output Cout
);

  wire cout_t, cs0, cs1, cs2, cs3, z0, z1, z2, z3;

  Multiplexer #(.width(4)) multiplexer_1 (.in0(Zero), .in1(Six), .out({cs3, cs2, cs1, cs0}), .sel(Cout));
  Adder_4bit Adder_4bit_1 (
    .cin(cin), .b0(b0), .b1(b1), .b2(b2), .b3(b3), .a0(a0), .a1(a1), .a2(a2), .a3(a3), .cout(cout_t),
    .s3(z3), .s2(z2), .s1(z1), .s0(z0));
  BCD_correction bcd_correction_1 (.k(cout_t), .z1(z1), .z2(z2), .z3(z3), .S1(Cout));
  Adder_4bit adder_4bit_1_dup2 (
    .cin(Zero_Cin), .b0(cs0), .b1(cs1), .b2(cs2), .b3(cs3), .a0(z0), .a1(z1), .a2(z2), .a3(z3),
    .cout(Zero_Cout), .s3(S03), .s2(S02), .s1(S01), .s0(S00));

  // Other names for the same wires on the sheet: mux_select = Cout
endmodule

module BCD_correction (
  input  k,
  input  z1,
  input  z2,
  input  z3,
  output S1
);

  wire and_1_out, and_2_out;

  and and_1 (and_1_out, z1, z3);
  and and_2 (and_2_out, z2, z3);
  or or_1 (S1, k, and_1_out, and_2_out);
endmodule

module Seg7_Decoder (
  input  i_m3,
  input  i_m2,
  input  i_m1,
  input  i_m0,
  output [7:0] o_seg
);

  wire and_1_out, and_2_out, and_3_out, and_4_out, and_5_out, and_6_out, and_7_out, and_8_out, and_10_out,
       and_11_out, and_12_out, and_13_out, not_1_out, not_2_out, not_3_out, not_4_out;

  not not_1 (not_1_out, i_m3);
  not not_2 (not_2_out, i_m2);
  not not_3 (not_3_out, i_m1);
  not not_4 (not_4_out, i_m0);
  and and_1 (and_1_out, not_1_out, not_2_out, not_3_out);
  and and_2 (and_2_out, i_m2, i_m1, i_m0);
  and and_3 (and_3_out, not_1_out, not_2_out, i_m0);
  and and_4 (and_4_out, not_2_out, i_m1);
  and and_5 (and_5_out, i_m2, not_3_out);
  and and_6 (and_6_out, not_1_out, not_2_out, not_3_out, i_m0);
  and and_7 (and_7_out, i_m2, not_3_out, not_4_out);
  and and_8 (and_8_out, i_m2, i_m1, i_m0);
  and and_9 (o_seg[2], not_2_out, i_m1, not_4_out);
  and and_10 (and_10_out, i_m2, not_3_out, i_m0);
  and and_11 (and_11_out, i_m2, i_m1, not_4_out);
  and and_12 (and_12_out, not_1_out, not_2_out, not_3_out, i_m0);
  and and_13 (and_13_out, i_m2, not_3_out, not_4_out);
  or or_1 (o_seg[6], and_1_out, and_2_out);
  or or_2 (o_seg[5], and_3_out, and_4_out);
  or or_3 (o_seg[4], i_m0, and_5_out);
  or or_4 (o_seg[3], and_6_out, and_7_out, and_8_out);
  or or_5 (o_seg[1], and_10_out, and_11_out);
  or or_6 (o_seg[0], and_12_out, and_13_out);

  assign o_seg[7] = 1'b1;
endmodule
