// Logisim project Lab_2_Solutions_Part7.circ as structural Verilog: 4 circuits, main circuit main
module main (
  input  in_1,
  input  v5,
  input  v4,
  input  v3,
  input  v2,
  input  v1,
  input  v0
);

  wire bcd_converter_1_d00, bcd_converter_1_d01, bcd_converter_1_d02, bcd_converter_1_d03,
       bcd_converter_1_d10, bcd_converter_1_d11, bcd_converter_1_d12, bcd_converter_1_d13, c0, c1, c2, c3,
       c4, c5, c6, s0, s1, s2, s3, s4, s5, s6;
  wire [7:7] Seg7_Decoder_1_o_seg, Seg_7_Decoder_2_o_seg;

  BCD_Converter bcd_converter_1 (
    .ADD_10(in_1), .v5(v5), .v4(v4), .v3(v3), .v2(v2), .v1(v1), .Zero(in_1), .v0(v0),
    .d13(bcd_converter_1_d13), .d12(bcd_converter_1_d12), .d11(bcd_converter_1_d11),
    .d10(bcd_converter_1_d10), .d03(bcd_converter_1_d03), .d02(bcd_converter_1_d02),
    .d01(bcd_converter_1_d01), .d00(bcd_converter_1_d00));
  Seg7_Decoder Seg7_Decoder_1 (
    .i_m3(bcd_converter_1_d13), .i_m2(bcd_converter_1_d12), .i_m1(bcd_converter_1_d11),
    .i_m0(bcd_converter_1_d10), .o_seg({Seg7_Decoder_1_o_seg[7], s6, s5, s4, s3, s2, s1, s0}));
  Seg7_Decoder Seg_7_Decoder_2 (
    .i_m3(bcd_converter_1_d03), .i_m2(bcd_converter_1_d02), .i_m1(bcd_converter_1_d01),
    .i_m0(bcd_converter_1_d00), .o_seg({Seg_7_Decoder_2_o_seg[7], c6, c5, c4, c3, c2, c1, c0}));
  _7_Segment_Display #(.active("false")) L_7_Segment_Display_2 (
    .g(s6), .f(s5), .a(s0), .b(s1), .e(s4), .d(s3), .c(s2), .dp(1'b1));
  _7_Segment_Display #(.active("false")) u_7_segment_display_1 (
    .g(c6), .f(c5), .a(c0), .b(c1), .e(c4), .d(c3), .c(c2), .dp(1'b1));
endmodule

module BCD_Converter (
  input  ADD_10,
  input  v5,
  input  v4,
  input  v3,
  input  v2,
  input  v1,
  input  Zero,
  input  v0,
  output d13,
  output d12,
  output d11,
  output d10,
  output d03,
  output d02,
  output d01,
  output d00
);

  wire m1y0, m1y1, m1y2, m2y0, m2y1, m2y2;

  add_3 Add1 (.x3(ADD_10), .x2(v5), .x1(v4), .x0(v3), .y3(d12), .y2(m1y2), .y1(m1y1), .y0(m1y0));
  add_3 Add2 (.x3(m1y2), .x2(m1y1), .x1(m1y0), .x0(v2), .y3(d11), .y2(m2y2), .y1(m2y1), .y0(m2y0));
  add_3 Add3 (.x3(m2y2), .x2(m2y1), .x1(m2y0), .x0(v1), .y3(d10), .y2(d03), .y1(d02), .y0(d01));

  assign d00 = v0;
  assign d13 = Zero;

  // Other names for the same wires on the sheet: m1y3 = d12; m2y3 = d11; m3y0 = d01; m3y1 = d02; m3y2 = d03;
  //   m3y3 = d10

  // Notes on the sheet:
  //   Tens
  //   Ones
endmodule

module add_3 (
  input  x3,
  input  x2,
  input  x1,
  input  x0,
  output y3,
  output y2,
  output y1,
  output y0
);

  wire and_1_out, and_2_out, and_3_out, and_4_out, and_5_out, and_6_out, and_7_out, and_8_out, and_9_out,
       and_10_out, not_1_out, not_2_out, not_3_out, not_4_out;

  not not_1 (not_1_out, x3);
  not not_2 (not_2_out, x2);
  not not_3 (not_3_out, x1);
  not not_4 (not_4_out, x0);
  and and_1 (and_1_out, x2, x0);
  and and_2 (and_2_out, x2, x1);
  and and_3 (and_3_out, x2, not_3_out, not_4_out);
  and and_4 (and_4_out, x3, x0);
  and and_5 (and_5_out, not_2_out, x1);
  and and_6 (and_6_out, x1, x0);
  and and_7 (and_7_out, x3, not_4_out);
  and and_8 (and_8_out, not_1_out, not_2_out, x0);
  and and_9 (and_9_out, x2, x1, not_4_out);
  and and_10 (and_10_out, x3, not_4_out);
  or or_1 (y3, and_1_out, and_2_out, x3);
  or or_2 (y2, and_3_out, and_4_out);
  or or_3 (y1, and_5_out, and_6_out, and_7_out);
  or or_4 (y0, and_8_out, and_9_out, and_10_out);
endmodule

module Seg7_Decoder (
  input  i_m3,
  input  i_m2,
  input  i_m1,
  input  i_m0,
  output [7:0] o_seg
);

  wire and_1_out, and_2_out, and_3_out, and_4_out, and_5_out, and_6_out, and_7_out, and_8_out, and_10_out,
       and_11_out, and_12_out, and_13_out, not_1_out, not_2_out, not_3_out, not_4_out;

  not not_1 (not_1_out, i_m3);
  not not_2 (not_2_out, i_m2);
  not not_3 (not_3_out, i_m1);
  not not_4 (not_4_out, i_m0);
  and and_1 (and_1_out, not_1_out, not_2_out, not_3_out);
  and and_2 (and_2_out, i_m2, i_m1, i_m0);
  and and_3 (and_3_out, not_1_out, not_2_out, i_m0);
  and and_4 (and_4_out, not_2_out, i_m1);
  and and_5 (and_5_out, i_m2, not_3_out);
  and and_6 (and_6_out, not_1_out, not_2_out, not_3_out, i_m0);
  and and_7 (and_7_out, i_m2, not_3_out, not_4_out);
  and and_8 (and_8_out, i_m2, i_m1, i_m0);
  and and_9 (o_seg[2], not_2_out, i_m1, not_4_out);
  and and_10 (and_10_out, i_m2, not_3_out, i_m0);
  and and_11 (and_11_out, i_m2, i_m1, not_4_out);
  and and_12 (and_12_out, not_1_out, not_2_out, not_3_out, i_m0);
  and and_13 (and_13_out, i_m2, not_3_out, not_4_out);
  or or_1 (o_seg[6], and_1_out, and_2_out);
  or or_2 (o_seg[5], and_3_out, and_4_out);
  or or_3 (o_seg[4], i_m0, and_5_out);
  or or_4 (o_seg[3], and_6_out, and_7_out, and_8_out);
  or or_5 (o_seg[1], and_10_out, and_11_out);
  or or_6 (o_seg[0], and_12_out, and_13_out);

  assign o_seg[7] = 1'b1;
endmodule
