// Logisim project Lab_4_Part_1.circ as structural Verilog: 1 circuit, main circuit main
module main (
  input  Enable,
  input  Reset,
  output out_3
);

  wire and_1_out, and_2_out, and_3_out, Clk_out, t_ff_1_q, t_ff_2_q, t_ff_3_q;

  Clock Clk (.out(Clk_out));
  T_Flip_Flop t_ff_1 (.T(Enable), .clk(Clk_out), .Q(t_ff_1_q), .reset(Reset));  // open: Qn, preset
  and and_1 (and_1_out, Enable, t_ff_1_q);
  T_Flip_Flop t_ff_2 (.T(and_1_out), .clk(Clk_out), .Q(t_ff_2_q), .reset(Reset));  // open: Qn, preset
  and and_2 (and_2_out, and_1_out, t_ff_2_q);
  T_Flip_Flop t_ff_3 (.T(and_2_out), .clk(Clk_out), .Q(t_ff_3_q), .reset(Reset));  // open: Qn, preset
  and and_3 (and_3_out, and_2_out, t_ff_3_q);
  T_Flip_Flop t_ff_4 (.T(and_3_out), .clk(Clk_out), .Q(out_3), .reset(Reset));  // open: Qn, preset

  // Notes on the sheet:
  //   LSB
  //   MSB
endmodule
