// Logisim project Lab_4_Part_5.circ as structural Verilog: 4 circuits, main circuit main
module main (
  input  Enable,
  input  Reset
);

  wire a0, a1, a2, a3, b0, b1, b2, b3, c0, c1, c2, c3, Clk_out, Counter_1_q0, Counter_1_q1, Counter_1_q2,
       Counter_1_q3, d0, d1, d2, d3, e0, e1, e2, e3, s0, s1, s2, s3, s4, s5, s6, t0, t1, t2, t3, t4, t5, t6,
       u0, u1, u2, u3, u4, u5, u6, v0, v1, v2, v3, v4, v5, v6, w0, w1, w2, w3, w4, w5, w6, x0, x1, x2, x3,
       y0, y1, y2, y3, y4, y5, y6;
  wire [7:7] D0_o_seg, D1_o_seg, D2_o_seg, D3_o_seg, D4_o_seg, D5_o_seg;

  Clock Clk (.out(Clk_out));
  Modulo_5_Counter Counter_1 (
    .Enable(Enable), .Clk(Clk_out), .Reset(Reset), .Q0(Counter_1_q0), .Q1(Counter_1_q1), .Q2(Counter_1_q2),
    .Q3(Counter_1_q3));
  Seven_Segment_Decoder u_D0 (
    .i_m3(e3), .i_m2(e2), .i_m1(e1), .i_m0(e0), .o_seg({D0_o_seg[7], s6, s5, s4, s3, s2, s1, s0}));
  Seven_Segment_Decoder u_D1 (
    .i_m3(d3), .i_m2(d2), .i_m1(d1), .i_m0(d0), .o_seg({D1_o_seg[7], t6, t5, t4, t3, t2, t1, t0}));
  Seven_Segment_Decoder u_D2 (
    .i_m3(c3), .i_m2(c2), .i_m1(c1), .i_m0(c0), .o_seg({D2_o_seg[7], u6, u5, u4, u3, u2, u1, u0}));
  Seven_Segment_Decoder u_D3 (
    .i_m3(b3), .i_m2(b2), .i_m1(b1), .i_m0(b0), .o_seg({D3_o_seg[7], v6, v5, v4, v3, v2, v1, v0}));
  Character_Encoding Encoder_1 (
    .q0(Counter_1_q0), .q1(Counter_1_q1), .q2(Counter_1_q2), .q3(Counter_1_q3), .HEX5({x3, x2, x1, x0}),
    .HEX4({a3, a2, a1, a0}), .HEX3({b3, b2, b1, b0}), .HEX2({c3, c2, c1, c0}), .HEX1({d3, d2, d1, d0}),
    .HEX0({e3, e2, e1, e0}));
  _7_Segment_Display #(.active("false")) HEX5 (.g(y6), .f(y5), .a(y0), .b(y1), .e(y4), .d(y3), .c(y2), .dp(1'b1));
  _7_Segment_Display #(.active("false")) HEX4 (.g(w6), .f(w5), .a(w0), .b(w1), .e(w4), .d(w3), .c(w2), .dp(1'b1));
  Seven_Segment_Decoder D5 (
    .i_m3(x3), .i_m2(x2), .i_m1(x1), .i_m0(x0), .o_seg({D5_o_seg[7], y6, y5, y4, y3, y2, y1, y0}));
  Seven_Segment_Decoder D4 (
    .i_m3(a3), .i_m2(a2), .i_m1(a1), .i_m0(a0), .o_seg({D4_o_seg[7], w6, w5, w4, w3, w2, w1, w0}));
  _7_Segment_Display #(.active("false")) HEX3 (.g(v6), .f(v5), .a(v0), .b(v1), .e(v4), .d(v3), .c(v2), .dp(1'b1));
  _7_Segment_Display #(.active("false")) HEX2 (.g(u6), .f(u5), .a(u0), .b(u1), .e(u4), .d(u3), .c(u2), .dp(1'b1));
  _7_Segment_Display #(.active("false")) HEX1 (.g(t6), .f(t5), .a(t0), .b(t1), .e(t4), .d(t3), .c(t2), .dp(1'b1));
  _7_Segment_Display #(.active("false")) HEX0 (.g(s6), .f(s5), .a(s0), .b(s1), .e(s4), .d(s3), .c(s2), .dp(1'b1));

  // Notes on the sheet:
  //   HEX5
  //   HEX0
endmodule

module Modulo_5_Counter (
  input  Enable,
  input  Clk,
  input  Reset,
  output Q0,
  output Q1,
  output Q2,
  output Q3
);

  wire In1, In2, In3, not_1_out, not_2_out, S, T0, T1, T2, T3;

  T_Flip_Flop t_ff_1 (.T(T0), .clk(Clk), .Q(Q0), .reset(Reset));  // open: Qn, preset
  Multiplexer multiplexer_1 (.in0(Enable), .in1(1'b1), .out(T0), .sel(S));
  and and_1 (In1, Enable, Q0);
  T_Flip_Flop t_ff_2 (.T(T1), .clk(Clk), .Q(Q1), .reset(Reset));  // open: Qn, preset
  Multiplexer multiplexer_2 (.in0(In1), .in1(1'b0), .out(T1), .sel(S));
  not not_1 (not_1_out, Q2);
  not not_2 (not_2_out, Q1);
  and and_2 (In2, T1, Q1);
  T_Flip_Flop t_ff_3 (.T(T2), .clk(Clk), .Q(Q2), .reset(Reset));  // open: Qn, preset
  Multiplexer multiplexer_3 (.in0(In2), .in1(1'b1), .out(T2), .sel(S));
  and and_3 (S, Q3, not_1_out, not_2_out, Q0);
  and and_4 (In3, T2, Q2);
  T_Flip_Flop t_ff_4 (.T(T3), .clk(Clk), .Q(Q3), .reset(Reset));  // open: Qn, preset
  Multiplexer multiplexer_4 (.in0(In3), .in1(1'b1), .out(T3), .sel(S));

  // Other names for the same wires on the sheet: In0 = Enable

  // Notes on the sheet:
  //   LSB
  //   Compare to 9
  //   MSB
endmodule

module Seven_Segment_Decoder (
  input  i_m3,
  input  i_m2,
  input  i_m1,
  input  i_m0,
  output [7:0] o_seg
);

  wire and_1_out, and_2_out, and_6_out, and_7_out, and_8_out, not_1_out, not_2_out, not_3_out;

  not not_1 (not_1_out, i_m2);
  not not_2 (not_2_out, i_m1);
  not not_3 (not_3_out, i_m0);
  and and_1 (and_1_out, not_2_out, not_3_out);
  and and_2 (and_2_out, i_m1, i_m0);
  and and_3 (o_seg[5], not_1_out, not_2_out, not_3_out);
  and and_4 (o_seg[4], not_1_out, not_2_out, not_3_out);
  and and_5 (o_seg[3], not_1_out, not_2_out);
  and and_6 (and_6_out, not_1_out, not_3_out);
  and and_7 (and_7_out, not_1_out, not_3_out);
  and and_8 (and_8_out, not_1_out, not_2_out);
  or or_1 (o_seg[6], and_1_out, and_2_out);
  or or_2 (o_seg[2], and_6_out, i_m1);
  or or_3 (o_seg[1], and_7_out, i_m1);
  or or_4 (o_seg[0], and_8_out, i_m0);

  assign o_seg[7] = 1'b1;
endmodule

module Character_Encoding (
  input  q0,
  input  q1,
  input  q2,
  input  q3,
  output [3:0] HEX5,
  output [3:0] HEX4,
  output [3:0] HEX3,
  output [3:0] HEX2,
  output [3:0] HEX1,
  output [3:0] HEX0
);

  wire and_2_out, and_3_out, and_4_out, and_5_out, and_7_out, and_8_out, and_9_out, and_10_out, and_12_out,
       and_13_out, and_14_out, and_15_out, and_16_out, and_17_out, and_19_out, and_20_out, and_21_out,
       and_22_out, and_23_out, and_24_out, and_26_out, and_27_out, and_28_out, and_29_out, and_30_out,
       and_31_out, and_33_out, and_34_out, and_35_out, and_36_out, and_37_out, and_38_out, and_39_out,
       and_40_out, not_1_out, not_2_out, not_3_out, not_4_out;

  not not_1 (not_1_out, q3);
  not not_2 (not_2_out, q2);
  not not_3 (not_3_out, q1);
  not not_4 (not_4_out, q0);
  and and_1 (HEX5[2], q3, not_2_out, not_3_out, q0);
  and and_2 (and_2_out, not_1_out, q2, q1);
  and and_3 (and_3_out, q3, not_2_out, not_3_out, not_4_out);
  and and_4 (and_4_out, not_1_out, q2, q0);
  and and_5 (and_5_out, q3, not_2_out, not_3_out, not_4_out);
  and and_6 (HEX4[2], q3, not_2_out, not_3_out, not_4_out);
  and and_7 (and_7_out, not_1_out, q2, q0);
  and and_8 (and_8_out, not_1_out, q2, q1);
  and and_9 (and_9_out, not_1_out, q2, not_4_out);
  and and_10 (and_10_out, not_1_out, q2, q1);
  and and_11 (HEX3[2], not_1_out, q2, q1, q0);
  and and_12 (and_12_out, not_1_out, q2, not_3_out);
  and and_13 (and_13_out, not_1_out, q2, not_4_out);
  and and_14 (and_14_out, not_1_out, not_2_out, q1, q0);
  and and_15 (and_15_out, not_1_out, q2, not_3_out, q0);
  and and_16 (and_16_out, not_1_out, q2, q1, not_4_out);
  and and_17 (and_17_out, q3, not_2_out, not_3_out, q0);
  and and_18 (HEX2[2], not_1_out, q2, q1, not_4_out);
  and and_19 (and_19_out, not_1_out, not_2_out, q1, q0);
  and and_20 (and_20_out, not_1_out, q2, not_3_out);
  and and_21 (and_21_out, q3, not_2_out, not_3_out, q0);
  and and_22 (and_22_out, not_1_out, not_2_out, q1, not_4_out);
  and and_23 (and_23_out, not_1_out, q2, not_3_out);
  and and_24 (and_24_out, q3, not_2_out, not_3_out, not_4_out);
  and and_25 (HEX1[2], not_1_out, q2, not_3_out, q0);
  and and_26 (and_26_out, not_1_out, not_2_out, q1);
  and and_27 (and_27_out, not_1_out, q2, not_3_out, not_4_out);
  and and_28 (and_28_out, q3, not_2_out, not_3_out);
  and and_29 (and_29_out, not_1_out, q2, not_3_out, not_4_out);
  and and_30 (and_30_out, not_1_out, q1, q0);
  and and_31 (and_31_out, not_2_out, not_3_out, q0);
  and and_32 (HEX0[2], not_1_out, q2, not_3_out, not_4_out);
  and and_33 (and_33_out, not_1_out, not_2_out, q1);
  and and_34 (and_34_out, not_1_out, q1, q0);
  and and_35 (and_35_out, q3, not_2_out, not_3_out);
  and and_36 (and_36_out, not_1_out, not_2_out, q0);
  and and_37 (and_37_out, not_1_out, not_2_out, q1);
  and and_38 (and_38_out, not_1_out, q1, not_4_out);
  and and_39 (and_39_out, q3, not_2_out, not_3_out);
  and and_40 (and_40_out, not_1_out, not_2_out, not_4_out);
  or or_1 (HEX5[1], and_2_out, and_3_out);
  or or_2 (HEX5[0], and_4_out, and_5_out);
  or or_3 (HEX4[1], and_7_out, and_8_out);
  or or_4 (HEX4[0], and_9_out, and_10_out);
  or or_5 (HEX3[1], and_12_out, and_13_out);
  or or_6 (HEX3[0], and_14_out, and_15_out, and_16_out, and_17_out);
  or or_7 (HEX2[1], and_19_out, and_20_out, and_21_out);
  or or_8 (HEX2[0], and_22_out, and_23_out, and_24_out);
  or or_9 (HEX1[1], and_26_out, and_27_out, and_28_out);
  or or_10 (HEX1[0], and_29_out, and_30_out, and_31_out);
  or or_11 (HEX0[1], and_33_out, and_34_out, and_35_out, and_36_out);
  or or_12 (HEX0[0], and_37_out, and_38_out, and_39_out, and_40_out);

  assign HEX0[3] = 1'b0;
  assign HEX1[3] = 1'b0;
  assign HEX2[3] = 1'b0;
  assign HEX3[3] = 1'b0;
  assign HEX4[3] = 1'b0;
  assign HEX5[3] = 1'b0;
endmodule
